// Logisim project alu.circ as structural Verilog: 1 circuit, main circuit alu
module alu (
  input  [31:0] A,
  input  [31:0] B,
  input  [3:0] ALUSel,
  output [31:0] ALUResult
);

  wire [31:0] add0, and0, besl, mul0, mulh0, mulhu, or0, sll0, slt0, sra0, srl0, sub0, Unused, unused_t, xor0;

  Multiplexer #(.select(4), .width(32)) multiplexer_1 (
    .in0(add0), .in1(sll0), .in2(slt0), .in3(unused_t), .in4(xor0), .in5(srl0), .in6(or0), .in7(and0),
    .in8(mul0), .in9(mulh0), .in10(unused_t), .in11(mulhu), .in12(sub0), .in13(sra0), .in14(Unused),
    .in15(besl), .out(ALUResult), .sel(ALUSel));
  Adder #(.width(32)) adder_1 (.a(A), .b(B), .out(add0));  // open: cin, cout
  Shifter #(.width(32)) shifter_1 (.in(A), .\dist (B[4:0]), .out(sll0));

  // Notes on the sheet:
  //   INPUTS to your circuit
  //   DON'T CHANGE THE LOCATIONS OF THE INPUTS AND OUTPUTS!
  //   OUTPUT from your circuit
endmodule
